// Logisim project Braille to binary convertor.circ as structural Verilog
module Braille_to_binary (
  input  a,
  input  b,
  input  c,
  input  d,
  input  e,
  input  f,
  input  t,
  output Y5,
  output Y4,
  output Y3,
  output Y2,
  output Y1,
  output Y0
);

  wire and_1_out, and_2_out, and_3_out, and_4_out, and_5_out, and_6_out, and_7_out, and_8_out, and_9_out,
       and_10_out, and_11_out, and_12_out, and_13_out, and_14_out, and_15_out, and_16_out, and_17_out,
       and_18_out, and_19_out, and_20_out, and_21_out, and_22_out, and_23_out, and_24_out, and_25_out,
       and_26_out, and_27_out, and_28_out, and_29_out, and_30_out, and_31_out, and_32_out, and_33_out,
       and_34_out, and_35_out, and_36_out, and_37_out, and_38_out, and_39_out, and_40_out, and_41_out,
       and_42_out, and_43_out, and_44_out, and_45_out, and_46_out, and_47_out, not_1_out, not_2_out,
       not_3_out, not_4_out, not_5_out, not_6_out, not_7_out, not_8_out, not_9_out, not_10_out, not_11_out,
       not_12_out, not_13_out, not_14_out, not_15_out, not_16_out, not_17_out, not_18_out, not_19_out,
       not_20_out, not_21_out, not_22_out, not_23_out, not_24_out, not_25_out, not_26_out, not_27_out,
       not_28_out, not_29_out, not_30_out, not_31_out, not_32_out, not_33_out, not_34_out, not_35_out,
       not_36_out, not_37_out, not_38_out, not_39_out, not_40_out, not_41_out, not_42_out, not_43_out,
       not_44_out, not_45_out, not_46_out, not_47_out, not_48_out, not_49_out, not_50_out, not_51_out,
       not_52_out, not_53_out, not_54_out, not_55_out, not_56_out, not_57_out, not_58_out, not_59_out,
       not_60_out, not_61_out, not_62_out, not_63_out, not_64_out, not_65_out, not_66_out, not_67_out,
       not_68_out, not_69_out, not_70_out, not_71_out, not_72_out, not_73_out, not_74_out, not_75_out,
       not_76_out, not_77_out, not_78_out, not_79_out, not_80_out, not_81_out, not_82_out, not_83_out,
       not_84_out, not_85_out, not_86_out, not_87_out, not_88_out, not_89_out, not_90_out, not_91_out,
       not_92_out;

  and and_1 (and_1_out, d, f);
  and and_2 (and_2_out, b, f);
  not not_1 (not_1_out, a);
  not not_2 (not_2_out, d);
  not not_3 (not_3_out, b);
  not not_4 (not_4_out, d);
  not not_5 (not_5_out, f);
  not not_6 (not_6_out, f);
  not not_7 (not_7_out, c);
  not not_8 (not_8_out, e);
  not not_9 (not_9_out, b);
  not not_10 (not_10_out, d);
  not not_11 (not_11_out, a);
  not not_12 (not_12_out, d);
  not not_13 (not_13_out, t);
  not not_14 (not_14_out, a);
  not not_15 (not_15_out, d);
  not not_16 (not_16_out, t);
  not not_17 (not_17_out, b);
  not not_18 (not_18_out, e);
  not not_19 (not_19_out, t);
  not not_20 (not_20_out, a);
  not not_21 (not_21_out, d);
  not not_22 (not_22_out, t);
  not not_23 (not_23_out, d);
  not not_24 (not_24_out, e);
  not not_25 (not_25_out, b);
  not not_26 (not_26_out, f);
  not not_27 (not_27_out, b);
  not not_28 (not_28_out, d);
  not not_29 (not_29_out, c);
  not not_30 (not_30_out, e);
  not not_31 (not_31_out, c);
  not not_32 (not_32_out, f);
  not not_33 (not_33_out, a);
  not not_34 (not_34_out, d);
  not not_35 (not_35_out, e);
  not not_36 (not_36_out, t);
  not not_37 (not_37_out, a);
  not not_38 (not_38_out, e);
  not not_39 (not_39_out, f);
  not not_40 (not_40_out, b);
  not not_41 (not_41_out, c);
  not not_42 (not_42_out, e);
  not not_43 (not_43_out, b);
  not not_44 (not_44_out, c);
  not not_45 (not_45_out, d);
  not not_46 (not_46_out, t);
  not not_47 (not_47_out, d);
  not not_48 (not_48_out, f);
  not not_49 (not_49_out, c);
  not not_50 (not_50_out, d);
  not not_51 (not_51_out, e);
  not not_52 (not_52_out, b);
  not not_53 (not_53_out, t);
  not not_54 (not_54_out, a);
  not not_55 (not_55_out, b);
  not not_56 (not_56_out, e);
  not not_57 (not_57_out, t);
  not not_58 (not_58_out, a);
  not not_59 (not_59_out, c);
  not not_60 (not_60_out, e);
  not not_61 (not_61_out, f);
  not not_62 (not_62_out, t);
  not not_63 (not_63_out, a);
  not not_64 (not_64_out, d);
  not not_65 (not_65_out, t);
  not not_66 (not_66_out, b);
  not not_67 (not_67_out, c);
  not not_68 (not_68_out, t);
  not not_69 (not_69_out, c);
  not not_70 (not_70_out, d);
  not not_71 (not_71_out, t);
  not not_72 (not_72_out, a);
  not not_73 (not_73_out, d);
  not not_74 (not_74_out, a);
  not not_75 (not_75_out, e);
  not not_76 (not_76_out, f);
  not not_77 (not_77_out, b);
  not not_78 (not_78_out, b);
  not not_79 (not_79_out, e);
  not not_80 (not_80_out, a);
  not not_81 (not_81_out, t);
  not not_82 (not_82_out, b);
  not not_83 (not_83_out, d);
  not not_84 (not_84_out, d);
  not not_85 (not_85_out, c);
  not not_86 (not_86_out, f);
  not not_87 (not_87_out, a);
  not not_88 (not_88_out, t);
  not not_89 (not_89_out, d);
  not not_90 (not_90_out, e);
  not not_91 (not_91_out, f);
  not not_92 (not_92_out, t);
  or or_1 (Y5, and_1_out, and_2_out);
  and and_3 (and_3_out, not_1_out, not_2_out, t);
  and and_4 (and_4_out, not_3_out, not_4_out, e);
  and and_5 (and_5_out, e, not_5_out, t);
  and and_6 (and_6_out, c, d, not_6_out, t);
  and and_7 (and_7_out, not_7_out, not_8_out, t);
  and and_8 (and_8_out, not_9_out, not_10_out, f);
  and and_9 (and_9_out, not_11_out, not_12_out, e, not_13_out);
  and and_10 (and_10_out, not_14_out, c, not_15_out, not_16_out);
  and and_11 (and_11_out, not_17_out, c, d, not_18_out, not_19_out);
  and and_12 (and_12_out, not_20_out, b, not_21_out, not_22_out);
  and and_13 (and_13_out, b, c, e);
  and and_14 (and_14_out, a, not_23_out, not_24_out, t);
  and and_15 (and_15_out, a, not_25_out, d, e, not_26_out);
  and and_16 (and_16_out, not_27_out, not_28_out, e);
  and and_17 (and_17_out, not_29_out, d, not_30_out);
  and and_18 (and_18_out, b, not_31_out, not_32_out, t);
  and and_19 (and_19_out, not_33_out, b, d, e);
  and and_20 (and_20_out, a, b, c, not_34_out, not_35_out);
  and and_21 (and_21_out, a, b, c, not_36_out);
  and and_22 (and_22_out, not_37_out, not_38_out, not_39_out, t);
  and and_23 (and_23_out, not_40_out, not_41_out, not_42_out, t);
  and and_24 (and_24_out, not_43_out, f);
  and and_25 (and_25_out, b, not_44_out, not_45_out, not_46_out);
  and and_26 (and_26_out, b, not_47_out, e, not_48_out);
  and and_27 (and_27_out, b, not_49_out, d, e);
  and and_28 (and_28_out, a, c, not_50_out, not_51_out);
  and and_29 (and_29_out, a, not_52_out, c, d, e);
  and and_30 (and_30_out, a, b, c, not_53_out);
  and and_31 (and_31_out, not_54_out, not_55_out, not_56_out, not_57_out);
  and and_32 (and_32_out, not_58_out, not_59_out, not_60_out, not_61_out, not_62_out);
  and and_33 (and_33_out, not_63_out, not_64_out, not_65_out);
  and and_34 (and_34_out, not_66_out, not_67_out, not_68_out);
  and and_35 (and_35_out, not_69_out, not_70_out, not_71_out);
  and and_36 (and_36_out, not_72_out, not_73_out, e);
  and and_37 (and_37_out, not_74_out, d, not_75_out, not_76_out, t);
  and and_38 (and_38_out, not_77_out, d, f);
  and and_39 (and_39_out, not_78_out, c, not_79_out, t);
  and and_40 (and_40_out, not_80_out, c, f, not_81_out);
  and and_41 (and_41_out, not_82_out, c, not_83_out, e);
  and and_42 (and_42_out, b, not_84_out, f);
  and and_43 (and_43_out, b, not_85_out, d, not_86_out, t);
  and and_44 (and_44_out, not_87_out, b, c, e, not_88_out);
  and and_45 (and_45_out, a, c, not_89_out, not_90_out, t);
  and and_46 (and_46_out, a, b, d, e, not_91_out);
  and and_47 (and_47_out, a, b, c, d, not_92_out);
  or or_2 (Y4, and_3_out, and_4_out, and_5_out, and_6_out);
  or or_3 (Y2, and_16_out, and_17_out, and_18_out, and_19_out, and_20_out, and_21_out);
  or or_4 (Y3, and_7_out, and_8_out, and_9_out, and_10_out, and_11_out, and_12_out, and_13_out, and_14_out, and_15_out);
  or or_5 (Y1, and_22_out, and_23_out, and_24_out, and_25_out, and_26_out, and_27_out, and_28_out, and_29_out, and_30_out);
  or or_6 (Y0, and_31_out, and_32_out, and_33_out, and_34_out, and_35_out, and_36_out, and_37_out, and_38_out, and_39_out, and_40_out, and_41_out, and_42_out, and_43_out, and_44_out, and_45_out, and_46_out, and_47_out);
endmodule
