// Logisim project Braille-to-Binary.circ as structural Verilog
module Braille_to_Binary (
  input  a,
  input  b,
  input  t,
  input  c,
  input  d,
  input  e,
  input  f,
  output Y5,
  output Y4,
  output Y3,
  output Y2,
  output Y1,
  output Y0
);

  wire nand_1_out, nand_2_out, nand_3_out, nand_4_out, nand_5_out, nand_6_out, nand_7_out, nand_8_out,
       nand_9_out, nand_10_out, nand_11_out, nand_12_out, nand_13_out, nand_14_out, nand_15_out, nand_16_out,
       nand_17_out, nand_18_out, nand_19_out, nand_20_out, nand_21_out, nand_22_out, nand_23_out,
       nand_24_out, nand_25_out, nand_26_out, nand_27_out, nand_28_out, nand_29_out, nand_30_out,
       nand_31_out, nand_32_out, nand_33_out, nand_34_out, nand_35_out, nand_37_out, nand_38_out,
       nand_39_out, nand_40_out, nand_41_out, nand_42_out, nand_43_out, nand_44_out, nand_45_out,
       nand_46_out, nand_47_out, nand_48_out, nand_49_out, nand_50_out, nand_51_out, nand_52_out,
       nand_53_out, nand_54_out, nand_55_out, nand_56_out, nand_57_out, nand_58_out, nand_59_out,
       nand_60_out, nand_61_out, nand_62_out, nand_63_out, nand_64_out, nand_65_out, nand_66_out,
       nand_67_out, nand_68_out, nand_69_out, nand_70_out, nand_71_out, nand_72_out, nand_73_out,
       nand_74_out, nand_75_out, nand_76_out, nand_77_out, nand_78_out, nand_79_out, nand_80_out,
       nand_81_out, nand_82_out, nand_83_out, nand_84_out, nand_85_out, nand_86_out, nand_87_out,
       nand_88_out, nand_89_out, nand_90_out, nand_91_out, nand_92_out, nand_93_out, nand_94_out,
       nand_95_out, nand_96_out, nand_97_out, nand_98_out, nand_99_out, nand_100_out, nand_101_out,
       nand_102_out;

  nand nand_1 (nand_1_out, d, f);
  nand nand_2 (nand_2_out, b, f);
  nand nand_3 (nand_3_out, f, f);
  nand nand_4 (nand_4_out, b, b);
  nand nand_5 (nand_5_out, f, f);
  nand nand_6 (nand_6_out, b, b);
  nand nand_7 (nand_7_out, t, t);
  nand nand_8 (nand_8_out, d, d);
  nand nand_9 (nand_9_out, e, e);
  nand nand_10 (nand_10_out, c, c);
  nand nand_11 (nand_11_out, f, f);
  nand nand_12 (nand_12_out, d, d);
  nand nand_13 (nand_13_out, e, e);
  nand nand_14 (nand_14_out, t, t);
  nand nand_15 (nand_15_out, a, a);
  nand nand_16 (nand_16_out, e, e);
  nand nand_17 (nand_17_out, f, f);
  nand nand_18 (nand_18_out, b, b);
  nand nand_19 (nand_19_out, c, c);
  nand nand_20 (nand_20_out, e, e);
  nand nand_21 (nand_21_out, b, b);
  nand nand_22 (nand_22_out, c, c);
  nand nand_23 (nand_23_out, d, d);
  nand nand_24 (nand_24_out, t, t);
  nand nand_25 (nand_25_out, c, c);
  nand nand_26 (nand_26_out, f, f);
  nand nand_27 (nand_27_out, d, d);
  nand nand_28 (nand_28_out, e, e);
  nand nand_29 (nand_29_out, t, t);
  nand nand_30 (nand_30_out, a, a);
  nand nand_31 (nand_31_out, f, f);
  nand nand_32 (nand_32_out, c, c);
  nand nand_33 (nand_33_out, f, f);
  nand nand_34 (nand_34_out, d, d);
  nand nand_35 (nand_35_out, t, t);
  nand nand_36 (Y5, nand_1_out, nand_2_out);
  nand nand_37 (nand_37_out, a, a);
  nand nand_38 (nand_38_out, d, d);
  nand nand_39 (nand_39_out, b, b);
  nand nand_40 (nand_40_out, d, d);
  nand nand_41 (nand_41_out, f, f);
  nand nand_42 (nand_42_out, a, a);
  nand nand_43 (nand_43_out, d, d);
  nand nand_44 (nand_44_out, t, t);
  nand nand_45 (nand_45_out, c, c);
  nand nand_46 (nand_46_out, e, e);
  nand nand_47 (nand_47_out, b, b);
  nand nand_48 (nand_48_out, d, d);
  nand nand_49 (nand_49_out, a, a);
  nand nand_50 (nand_50_out, b, b);
  nand nand_51 (nand_51_out, d, d);
  nand nand_52 (nand_52_out, c, c);
  nand nand_53 (nand_53_out, e, e);
  nand nand_54 (nand_54_out, b, b);
  nand nand_55 (nand_55_out, a, a);
  nand nand_56 (nand_56_out, d, d);
  nand nand_57 (nand_57_out, t, t);
  nand nand_58 (nand_58_out, b, b);
  nand nand_59 (nand_59_out, c, c);
  nand nand_60 (nand_60_out, t, t);
  nand nand_61 (nand_61_out, c, c);
  nand nand_62 (nand_62_out, d, d);
  nand nand_63 (nand_63_out, t, t);
  nand nand_64 (nand_64_out, b, b);
  nand nand_65 (nand_65_out, b, b);
  nand nand_66 (nand_66_out, d, d);
  nand nand_67 (nand_67_out, nand_37_out, nand_38_out, t);
  nand nand_68 (nand_68_out, nand_39_out, nand_40_out, e);
  nand nand_69 (nand_69_out, e, nand_41_out);
  nand nand_70 (nand_70_out, c, d, nand_3_out, t);
  nand nand_71 (nand_71_out, nand_42_out, nand_43_out, nand_44_out);
  nand nand_72 (nand_72_out, nand_45_out, nand_46_out, t);
  nand nand_73 (nand_73_out, nand_47_out, nand_48_out, f);
  nand nand_74 (nand_74_out, nand_4_out, d, e, nand_5_out);
  nand nand_75 (nand_75_out, nand_6_out, c, d, nand_7_out);
  nand nand_76 (nand_76_out, b, c, e);
  nand nand_77 (nand_77_out, a, nand_8_out, nand_9_out, t);
  nand nand_78 (nand_78_out, nand_49_out, e);
  nand nand_79 (nand_79_out, nand_50_out, nand_51_out, e);
  nand nand_80 (nand_80_out, nand_52_out, d, nand_53_out);
  nand nand_81 (nand_81_out, b, nand_10_out, nand_11_out, t);
  nand nand_82 (nand_82_out, a, b, c, nand_12_out, nand_13_out);
  nand nand_83 (nand_83_out, a, b, c, nand_14_out);
  nand nand_84 (nand_84_out, nand_15_out, nand_16_out, nand_17_out, t);
  nand nand_85 (nand_85_out, nand_18_out, nand_19_out, nand_20_out, t);
  nand nand_86 (nand_86_out, nand_54_out, f);
  nand nand_87 (nand_87_out, nand_21_out, c, d, e);
  nand nand_88 (nand_88_out, b, nand_22_out, nand_23_out, nand_24_out);
  nand nand_89 (nand_89_out, b, nand_25_out, e, nand_26_out);
  nand nand_90 (nand_90_out, a, c, nand_27_out, nand_28_out);
  nand nand_91 (nand_91_out, a, b, d, e);
  nand nand_92 (nand_92_out, a, b, c, nand_29_out);
  nand nand_93 (nand_93_out, nand_55_out, nand_56_out, nand_57_out);
  nand nand_94 (nand_94_out, nand_58_out, nand_59_out, nand_60_out);
  nand nand_95 (nand_95_out, nand_61_out, nand_62_out, nand_63_out);
  nand nand_96 (nand_96_out, nand_30_out, d, nand_31_out, t);
  nand nand_97 (nand_97_out, nand_64_out, d, f);
  nand nand_98 (nand_98_out, nand_65_out, c, t);
  nand nand_99 (nand_99_out, b, nand_66_out, f);
  nand nand_100 (nand_100_out, b, nand_32_out, d, nand_33_out, t);
  nand nand_101 (nand_101_out, a, c, nand_34_out, t);
  nand nand_102 (nand_102_out, a, b, c, d, nand_35_out);
  nand nand_103 (Y4, nand_67_out, nand_68_out, nand_69_out, nand_70_out);
  nand nand_104 (Y3, nand_71_out, nand_72_out, nand_73_out, nand_74_out, nand_75_out, nand_76_out, nand_77_out);
  nand nand_105 (Y2, nand_78_out, nand_79_out, nand_80_out, nand_81_out, nand_82_out, nand_83_out);
  nand nand_106 (Y1, nand_84_out, nand_85_out, nand_86_out, nand_87_out, nand_88_out, nand_89_out, nand_90_out, nand_91_out, nand_92_out);
  nand nand_107 (Y0, nand_93_out, nand_94_out, nand_95_out, nand_96_out, nand_97_out, nand_98_out, nand_99_out, nand_100_out, nand_101_out, nand_102_out);
endmodule
